# Fritzing sketch blink_schem (saved by Fritzing 0.9.6b)
breadboards: 1

parts:
  LED = LED - 5mm [color="Red (633nm)" package="5 mm [THT]"]
  R1 = Resistor [tolerance=±5% resistance=220 power=0.25 package=THT]

nets:
  GND/ground: LED.cathode
  N1: LED.anode, R1.Pin_1
  GPIO: R1.Pin_0

notes:
  Anode
  Cathode
  (long lead)
